// Logisim project 2023 CPU-AC v.0.circ as structural Verilog: 22 circuits, main circuit Sumador-Restador 4 bits
module Semisumador_1_bit (
  input  A,
  input  B,
  output Resultado,
  output Acarreo_out
);

  and and_1 (Acarreo_out, A, B);
  xor xor_1 (Resultado, A, B);

  // Notes on the sheet:
  //   Semisumador
  //   A
  //   B
  //   0
  //   0
  //   0
  //   1
  //   1
  //   0
  //   1
  //   1
  //   AND
  //   0
  //   0
  //   0
  //   1
  //   B
  //   A
  //   0
  //   0
  //   0
  //   0
  //   1
  //   0
  //   1
  //   0
  //   0
  //   1
  //   1
  //   1
  //   XOR
  //   A
  //   B
  //   0
  //   0
  //   0
  //   0
  //   1
  //   1
  //   1
  //   0
  //   1
  //   1
  //   1
  //   0
  //   Acarreo-out
  //   Resultado
  //   0
  //   1
  //   1
  //   0
  //   = 0
  //   = 1
  //   = 1
  //   = 2
endmodule

module Sumadorcompleto_1_bit (
  input  Acarreo_in,
  input  A,
  input  B,
  output Resultado,
  output Acarreo_out
);

  wire and_1_out, and_2_out, xor_1_out;

  and and_1 (and_1_out, A, B);
  xor xor_1 (xor_1_out, A, B);
  or or_1 (Acarreo_out, and_1_out, and_2_out);
  and and_2 (and_2_out, Acarreo_in, xor_1_out);
  xor xor_2 (Resultado, Acarreo_in, xor_1_out);

  // Notes on the sheet:
  //   Semisumador
  //   Sumador completo
  //   Semisumador
endmodule

module Sumador_Restador_4_bits (
  input  Op,
  input  [3:0] A,
  input  [3:0] B,
  output [3:0] Resultado,
  output Acarreo_out
);

  wire sumadorcompleto_1_bit_1_acarreo_out, sumadorcompleto_1_bit_2_acarreo_out,
       sumadorcompleto_1_bit_3_acarreo_out, xor_1_out, xor_2_out, xor_3_out, xor_4_out;

  // Probe on A
  // Probe on B
  // Probe on A
  // Probe on B
  xor xor_1 (xor_1_out, Op, B[3]);
  xor xor_2 (xor_2_out, Op, B[2]);
  xor xor_3 (xor_3_out, Op, B[1]);
  xor xor_4 (xor_4_out, Op, B[0]);
  Sumadorcompleto_1_bit sumadorcompleto_1_bit_1 (
    .A(A[0]), .B(xor_4_out), .Resultado(Resultado[0]), .Acarreo_out(sumadorcompleto_1_bit_1_acarreo_out),
    .Acarreo_in(Op));
  Sumadorcompleto_1_bit sumadorcompleto_1_bit_2 (
    .A(A[1]), .B(xor_3_out), .Resultado(Resultado[1]), .Acarreo_out(sumadorcompleto_1_bit_2_acarreo_out),
    .Acarreo_in(sumadorcompleto_1_bit_1_acarreo_out));
  Sumadorcompleto_1_bit sumadorcompleto_1_bit_3 (
    .A(A[2]), .B(xor_2_out), .Resultado(Resultado[2]), .Acarreo_out(sumadorcompleto_1_bit_3_acarreo_out),
    .Acarreo_in(sumadorcompleto_1_bit_2_acarreo_out));
  Sumadorcompleto_1_bit sumadorcompleto_1_bit_4 (
    .A(A[3]), .B(xor_1_out), .Resultado(Resultado[3]), .Acarreo_out(Acarreo_out),
    .Acarreo_in(sumadorcompleto_1_bit_3_acarreo_out));
  // Probe on Resultado
  // Probe on Resultado

  // Notes on the sheet:
  //   Acarreo-in
  //   0
  //   1
  //   Op
  //   Sumar
  //   Restar
endmodule

module Sumador_Restador_8_bits (
  input  Op,
  input  [7:0] A,
  input  [7:0] B,
  output [7:0] Resultado,
  output Acarreo_out
);

  wire sumadorcompleto_1_bit_1_acarreo_out, sumadorcompleto_1_bit_2_acarreo_out,
       sumadorcompleto_1_bit_3_acarreo_out, sumadorcompleto_1_bit_4_acarreo_out,
       sumadorcompleto_1_bit_5_acarreo_out, sumadorcompleto_1_bit_6_acarreo_out,
       sumadorcompleto_1_bit_7_acarreo_out, xor_1_out, xor_2_out, xor_3_out, xor_4_out, xor_5_out, xor_6_out,
       xor_7_out, xor_8_out;

  // Probe on A
  // Probe on B
  // Probe on A
  // Probe on B
  xor xor_1 (xor_1_out, Op, B[7]);
  xor xor_2 (xor_2_out, Op, B[6]);
  xor xor_3 (xor_3_out, Op, B[5]);
  xor xor_4 (xor_4_out, Op, B[4]);
  xor xor_5 (xor_5_out, Op, B[3]);
  xor xor_6 (xor_6_out, Op, B[2]);
  xor xor_7 (xor_7_out, Op, B[1]);
  xor xor_8 (xor_8_out, Op, B[0]);
  Sumadorcompleto_1_bit sumadorcompleto_1_bit_1 (
    .A(A[0]), .B(xor_8_out), .Resultado(Resultado[0]), .Acarreo_out(sumadorcompleto_1_bit_1_acarreo_out),
    .Acarreo_in(Op));
  Sumadorcompleto_1_bit sumadorcompleto_1_bit_2 (
    .A(A[1]), .B(xor_7_out), .Resultado(Resultado[1]), .Acarreo_out(sumadorcompleto_1_bit_2_acarreo_out),
    .Acarreo_in(sumadorcompleto_1_bit_1_acarreo_out));
  Sumadorcompleto_1_bit sumadorcompleto_1_bit_3 (
    .A(A[2]), .B(xor_6_out), .Resultado(Resultado[2]), .Acarreo_out(sumadorcompleto_1_bit_3_acarreo_out),
    .Acarreo_in(sumadorcompleto_1_bit_2_acarreo_out));
  Sumadorcompleto_1_bit sumadorcompleto_1_bit_4 (
    .A(A[3]), .B(xor_5_out), .Resultado(Resultado[3]), .Acarreo_out(sumadorcompleto_1_bit_4_acarreo_out),
    .Acarreo_in(sumadorcompleto_1_bit_3_acarreo_out));
  Sumadorcompleto_1_bit sumadorcompleto_1_bit_5 (
    .A(A[4]), .B(xor_4_out), .Resultado(Resultado[4]), .Acarreo_out(sumadorcompleto_1_bit_5_acarreo_out),
    .Acarreo_in(sumadorcompleto_1_bit_4_acarreo_out));
  Sumadorcompleto_1_bit sumadorcompleto_1_bit_6 (
    .A(A[5]), .B(xor_3_out), .Resultado(Resultado[5]), .Acarreo_out(sumadorcompleto_1_bit_6_acarreo_out),
    .Acarreo_in(sumadorcompleto_1_bit_5_acarreo_out));
  Sumadorcompleto_1_bit sumadorcompleto_1_bit_7 (
    .A(A[6]), .B(xor_2_out), .Resultado(Resultado[6]), .Acarreo_out(sumadorcompleto_1_bit_7_acarreo_out),
    .Acarreo_in(sumadorcompleto_1_bit_6_acarreo_out));
  Sumadorcompleto_1_bit sumadorcompleto_1_bit_8 (
    .A(A[7]), .B(xor_1_out), .Resultado(Resultado[7]), .Acarreo_out(Acarreo_out),
    .Acarreo_in(sumadorcompleto_1_bit_7_acarreo_out));
  // Probe on Resultado
  // Probe on Resultado

  // Notes on the sheet:
  //   Acarreo-in
  //   0
  //   1
  //   Op
  //   Sumar
  //   Restar
endmodule

module Sumador_Restador_con_flags (
  input  Op,
  input  [7:0] A,
  input  [7:0] B,
  output Acarreo__Carry,
  output Cero__Zero,
  output [7:0] Resultado
);

  wire A_Out, not_1_out, sumadorcompleto_1_bit_1_acarreo_out, sumadorcompleto_1_bit_2_acarreo_out,
       sumadorcompleto_1_bit_3_acarreo_out, sumadorcompleto_1_bit_4_acarreo_out,
       sumadorcompleto_1_bit_5_acarreo_out, sumadorcompleto_1_bit_6_acarreo_out,
       sumadorcompleto_1_bit_7_acarreo_out, xor_1_out, xor_2_out, xor_3_out, xor_4_out, xor_5_out, xor_6_out,
       xor_7_out, xor_8_out;

  // Probe on A
  // Probe on B
  // Probe on A
  // Probe on B
  xor xor_1 (xor_1_out, Op, B[7]);
  xor xor_2 (xor_2_out, Op, B[6]);
  xor xor_3 (xor_3_out, Op, B[5]);
  xor xor_4 (xor_4_out, Op, B[4]);
  xor xor_5 (xor_5_out, Op, B[3]);
  xor xor_6 (xor_6_out, Op, B[2]);
  xor xor_7 (xor_7_out, Op, B[1]);
  xor xor_8 (xor_8_out, Op, B[0]);
  Sumadorcompleto_1_bit sumadorcompleto_1_bit_1 (
    .A(A[0]), .B(xor_8_out), .Resultado(Resultado[0]), .Acarreo_out(sumadorcompleto_1_bit_1_acarreo_out),
    .Acarreo_in(Op));
  Sumadorcompleto_1_bit sumadorcompleto_1_bit_2 (
    .A(A[1]), .B(xor_7_out), .Resultado(Resultado[1]), .Acarreo_out(sumadorcompleto_1_bit_2_acarreo_out),
    .Acarreo_in(sumadorcompleto_1_bit_1_acarreo_out));
  Sumadorcompleto_1_bit sumadorcompleto_1_bit_3 (
    .A(A[2]), .B(xor_6_out), .Resultado(Resultado[2]), .Acarreo_out(sumadorcompleto_1_bit_3_acarreo_out),
    .Acarreo_in(sumadorcompleto_1_bit_2_acarreo_out));
  Sumadorcompleto_1_bit sumadorcompleto_1_bit_4 (
    .A(A[3]), .B(xor_5_out), .Resultado(Resultado[3]), .Acarreo_out(sumadorcompleto_1_bit_4_acarreo_out),
    .Acarreo_in(sumadorcompleto_1_bit_3_acarreo_out));
  Sumadorcompleto_1_bit sumadorcompleto_1_bit_5 (
    .A(A[4]), .B(xor_4_out), .Resultado(Resultado[4]), .Acarreo_out(sumadorcompleto_1_bit_5_acarreo_out),
    .Acarreo_in(sumadorcompleto_1_bit_4_acarreo_out));
  Sumadorcompleto_1_bit sumadorcompleto_1_bit_6 (
    .A(A[5]), .B(xor_3_out), .Resultado(Resultado[5]), .Acarreo_out(sumadorcompleto_1_bit_6_acarreo_out),
    .Acarreo_in(sumadorcompleto_1_bit_5_acarreo_out));
  Sumadorcompleto_1_bit sumadorcompleto_1_bit_7 (
    .A(A[6]), .B(xor_2_out), .Resultado(Resultado[6]), .Acarreo_out(sumadorcompleto_1_bit_7_acarreo_out),
    .Acarreo_in(sumadorcompleto_1_bit_6_acarreo_out));
  Sumadorcompleto_1_bit sumadorcompleto_1_bit_8 (
    .A(A[7]), .B(xor_1_out), .Resultado(Resultado[7]), .Acarreo_out(A_Out),
    .Acarreo_in(sumadorcompleto_1_bit_7_acarreo_out));
  not not_1 (not_1_out, A_Out);
  nor nor_1 (Cero__Zero, Resultado[0], Resultado[1], Resultado[2], Resultado[3], Resultado[4], Resultado[5], Resultado[6], Resultado[7]);
  // Probe on Resultado
  Multiplexer #(.enable("false")) multiplexer_1 (.in0(A_Out), .in1(not_1_out), .out(Acarreo__Carry), .sel(Op));
  // Probe on Resultado

  // Notes on the sheet:
  //   Acarreo-in
  //   0
  //   1
  //   Op
  //   Sumar
  //   Restar
  //   En la operación restar A+(-B) --> Acarreo =1, si A+(-B) está dentro del rango {0..255}
  //   Se cambia el comportamiento del Acarreo =1 en la operación restar --> Acerreo = 1, si A+(-B) < 0
  //   Para la operación +/- el acarreo = 1, si el resultado cae fuera del rango{0..255}
  //   En la operación sumar A+B --> Acarreo =1 si A+B > 255
  //   {0..255}
  //   Rango de valores enteros representables con 8 bits sin signo
  //   Entonces A<B porque A +(-B) <0 
  //   Funciona así:
  //   Si Acarreo (Carry) = 1:  A >= B
  //   Si Acarreo (Carry) = 0:  A < B 
  //   Pero queremos que funcione así:
  //   Si Acarreo (Carry) = 1:  A < B 
  //   A<B --> C=1
  //   Si Acarreo (Carry) = 0:  A >= B
endmodule

module Sim_AC_1 (
  input  Clock,
  input  [7:0] Dato_desde_memoria,
  input  ALUOp
);

  wire [7:0] register_1_q, sumador_restador_8_bits_1_resultado;

  // Probe on sumador_restador_8_bits_1_resultado
  // Probe on sumador_restador_8_bits_1_resultado
  Register #(.trigger("falling")) register_1 (
    .D(sumador_restador_8_bits_1_resultado), .Q(register_1_q), .clk(Clock));  // open: en, clr
  // Probe on sumador_restador_8_bits_1_resultado
  // Probe on register_1_q
  // Probe on register_1_q
  // Probe on register_1_q
  // Probe on Dato_desde_memoria
  // Probe on Dato_desde_memoria
  // Probe on Dato_desde_memoria
  Sumador_Restador_8_bits sumador_restador_8_bits_1 (
    .Op(ALUOp), .A(register_1_q), .B(Dato_desde_memoria), .Resultado(sumador_restador_8_bits_1_resultado));  // open: Acarreo_out

  // Notes on the sheet:
  //   Set de instrucciones
  //   Operaciones
  //   ADD
  //   SUB
  //   Sim-AC-1
  //   CodeOp
  //   0
  //   0
  //   0 =
  //   1
  //   1
  //   1 =
  //   ALUOp
  //   Registro
  //   Registro AC: ACumulador
  //   AC
  //   ALUOp
  //   AC: registro ACumulador se escribe por flanco descendente o de bajada
endmodule

module Sim_AC_2_Harvard (
  input  Clock,
  input  [4:0] \Dirección 
);

  wire [7:0] multiplexer_1_out, ram_1_data, ram_2_data, register_1_q, sumador_restador_8_bits_1_resultado;

  // Probe on \Dirección 
  // Probe on \Dirección 
  RAM #(.addrWidth(5)) ram_1 (.addr(\Dirección ), .data(ram_1_data));  // open: sel, clk, ld, clr
  // Probe on ram_1_data[4:0]
  // Probe on ram_1_data[4:0]
  // Probe on ram_1_data[7:5]
  // Probe on ram_1_data[7:5]
  Register #(.trigger("falling")) register_1 (
    .D(sumador_restador_8_bits_1_resultado), .Q(register_1_q), .clk(Clock));  // open: en, clr
  // Probe on sumador_restador_8_bits_1_resultado
  // Probe on sumador_restador_8_bits_1_resultado
  // Probe on sumador_restador_8_bits_1_resultado
  Multiplexer #(.width(8), .enable("false")) multiplexer_1 (
    .in0(register_1_q), .in1({8{1'b0}}), .out(multiplexer_1_out), .sel(ram_1_data[6]));
  // Probe on multiplexer_1_out
  // Probe on multiplexer_1_out
  // Probe on multiplexer_1_out
  // Probe on ram_2_data
  // Probe on ram_2_data
  // Probe on ram_2_data
  Sumador_Restador_8_bits sumador_restador_8_bits_1 (
    .Op(ram_1_data[5]), .A(multiplexer_1_out), .B(ram_2_data), .Resultado(sumador_restador_8_bits_1_resultado));  // open: Acarreo_out
  RAM #(.addrWidth(5), .bus("separate")) ram_2 (
    .addr(ram_1_data[4:0]), .data(ram_2_data));  // open: din, str, sel, clk, ld, clr

  // Notes on the sheet:
  //   Sintaxis
  //   ADD [dirección]
  //   SUB [dirección]
  //   LDA [dirección]
  //   Set de instrucciones
  //   La [dirección] es una posición de la memoria de datos
  //   LDA [dirección] = LOAD ACCUMULATOR
  //   CodeOp
  //   000
  //   0 =
  //   1 =
  //   001
  //   2 =
  //   010
  //   Sim-AC-2-Harvard
  //   AluY
  //   ALUOp
  //   0
  //   0
  //   0
  //   1
  //   1
  //   0
  //   Formato Instrucción
  //   CodeOp
  //   | b7 b6  b5 | b4 b3 b2 b1 b0 | 
  //   (byte 1)
  //   Dirección
  //   LDA [0]
  //   0
  //   ADD [1]
  //   1
  //   LDA [2]
  //   2
  //   SUB [3]
  //   3
  //   !!Cantidad de posiciones direccionables 2**5 = 32 posiciones
  //   Memoria de instrucciones
  //   ProgramaAC-1.mem
  //    = 0x40 hex
  //    = 0x01 hex
  //    = 0x42 hex
  //    = 0x23 hex
  //   Dirección
  //   CodeOp
  //   AC
  //   Arquitectura Harvard
  //   Memoria de datos e intrucciones separadas
  //   AluY
  //   ALUOp
  //   0x02 hex
  //   0
  //   0x03 hex
  //   1
  //   0x05 hex
  //   2
  //   0x01 hex
  //   3
  //   Memoria de datos
  //   DatosAC-1.mem
endmodule

module Sim_AC_2_Von_Neumann (
  input  Clock,
  input  [4:0] PC
);

  wire [2:0] register_1_q_2;
  wire [4:0] multiplexer_1_out, register_1_q;
  wire [7:0] multiplexer_2_out, ram_1_data, register_2_q, sumador_restador_8_bits_1_resultado;

  // Probe on PC
  // Probe on PC
  // Probe on register_1_q
  // Probe on register_1_q
  Multiplexer #(.width(5), .enable("false")) multiplexer_1 (
    .in0(PC), .in1(register_1_q), .out(multiplexer_1_out), .sel(Clock));
  RAM #(.addrWidth(5)) ram_1 (.addr(multiplexer_1_out), .data(ram_1_data));  // open: sel, clk, ld, clr
  Register register_1 (.D(ram_1_data), .Q({register_1_q_2, register_1_q}), .clk(Clock));  // open: en, clr
  // Probe on register_1_q_2
  // Probe on register_1_q_2
  Register #(.trigger("falling")) register_2 (
    .D(sumador_restador_8_bits_1_resultado), .Q(register_2_q), .clk(Clock));  // open: en, clr
  // Probe on sumador_restador_8_bits_1_resultado
  // Probe on sumador_restador_8_bits_1_resultado
  // Probe on sumador_restador_8_bits_1_resultado
  Multiplexer #(.width(8), .enable("false")) multiplexer_2 (
    .in0(register_2_q), .in1({8{1'b0}}), .out(multiplexer_2_out), .sel(register_1_q_2[1]));
  // Probe on multiplexer_2_out
  // Probe on multiplexer_2_out
  // Probe on multiplexer_2_out
  // Probe on ram_1_data
  // Probe on ram_1_data
  // Probe on ram_1_data
  Sumador_Restador_8_bits sumador_restador_8_bits_1 (
    .Op(register_1_q_2[0]), .A(multiplexer_2_out), .B(ram_1_data),
    .Resultado(sumador_restador_8_bits_1_resultado));  // open: Acarreo_out

  // Other names for the same wires on the sheet: SelPC_Data = Clock

  // Notes on the sheet:
  //   Sintaxis
  //   ADD [dirección]
  //   SUB [dirección]
  //   LDA [dirección]
  //   0
  //   1
  //   2
  //   3
  //   4
  //   5
  //   6
  //   7
  //   Set de instrucciones
  //   La [dirección] es una posición de la memoria de datos
  //   LDA [dirección] = LOAD ACCUMULATOR
  //   Clock = 0 => Capta instrucción
  //   LDA [4]
  //   ADD [5]
  //   LDA [6]
  //   SUB [7]
  //   0x02 hex
  //   0x03 hex
  //   0x04 hex
  //   0x01 hex
  //   CodeOp
  //   000
  //   0 =
  //   1 =
  //   001
  //   2 =
  //   010
  //   Clock = 1 => Obtiene operando y ejecuta
  //   ProgramaAC-VonNeumann.mem
  //    = 0x44 hex
  //    = 0x05 hex
  //    = 0x46 hex
  //    = 0x27 hex
  //   Sim-AC-2-Von Neumann
  //   ALUOp
  //   AluY
  //   0
  //   0
  //   0
  //   1
  //   1
  //   0
  //   CodeOp
  //   Si clock es cero selecciona el PC
  //   Si clock es uno selecciona la direccón
  //   Formato Instrucción
  //   Dirección
  //   | b7 b6  b5 | b4 b3 b2 b1 b0 | 
  //   !!Cantidad de posiciones direccionables 2**5 = 32 posiciones
  //   (byte 1)
  //   Memoria de instrucciones y datos
  //   El registro IR se escibe por flanco ascendente o de subida (Rising edge)
  //   Arquitectura Von Neumann
  //   Memoria de datos e intrucciones juntas
  //   IR
  //   AC
  //   CodeOp
  //   AluY
  //   ALUOp
endmodule

module Sim_AC_3_Harvard (
  input  Clock
);

  wire [4:0] adder_1_out, register_1_q;
  wire [7:0] multiplexer_1_out, ram_1_data, ram_2_data, register_2_q, sumador_restador_8_bits_1_resultado;

  Adder #(.width(5)) adder_1 (.a(register_1_q), .b(5'b00001), .out(adder_1_out));  // open: cin, cout
  // Probe on register_1_q
  // Probe on adder_1_out
  Register #(.width(5), .trigger("falling")) register_1 (
    .D(adder_1_out), .Q(register_1_q), .clk(Clock));  // open: en, clr
  // Probe on register_1_q
  // Probe on register_1_q
  RAM #(.addrWidth(5)) ram_1 (.addr(register_1_q), .data(ram_1_data));  // open: sel, clk, ld, clr
  // Probe on ram_1_data[4:0]
  // Probe on ram_1_data[4:0]
  // Probe on ram_1_data[7:5]
  // Probe on ram_1_data[7:5]
  Register #(.trigger("falling")) register_2 (
    .D(sumador_restador_8_bits_1_resultado), .Q(register_2_q), .clk(Clock));  // open: en, clr
  // Probe on sumador_restador_8_bits_1_resultado
  // Probe on sumador_restador_8_bits_1_resultado
  // Probe on sumador_restador_8_bits_1_resultado
  Multiplexer #(.width(8), .enable("false")) multiplexer_1 (
    .in0(register_2_q), .in1({8{1'b0}}), .out(multiplexer_1_out), .sel(ram_1_data[6]));
  // Probe on multiplexer_1_out
  // Probe on multiplexer_1_out
  // Probe on multiplexer_1_out
  // Probe on ram_2_data
  // Probe on ram_2_data
  // Probe on ram_2_data
  Sumador_Restador_8_bits sumador_restador_8_bits_1 (
    .Op(ram_1_data[5]), .A(multiplexer_1_out), .B(ram_2_data), .Resultado(sumador_restador_8_bits_1_resultado));  // open: Acarreo_out
  RAM #(.addrWidth(5), .bus("separate")) ram_2 (
    .addr(ram_1_data[4:0]), .data(ram_2_data));  // open: din, str, sel, clk, ld, clr

  // Notes on the sheet:
  //   Sintaxis
  //   Set de instrucciones
  //   ADD [dirección]
  //   SUB [dirección]
  //   LDA [dirección]
  //   0 =
  //   1 =
  //   2 =
  //   CodeOp
  //   000
  //   001
  //   010
  //   Sim-AC-3-Harvard
  //   ALUOp
  //   AluY
  //   0
  //   0
  //   0
  //   1
  //   1
  //   0
  //   Registro PC =
  //   Program Counter
  //    PC + 1
  //   CodeOp
  //    El registro PC y AC se escribe por flanco descendente o de bajada (Falling edge)
  //   PC
  //   Formato Instrucción
  //   Dirección
  //   | b7 b6  b5 | b4 b3 b2 b1 b0 | 
  //   (byte 1)
  //   LDA [0]
  //   0
  //   ADD [1]
  //   1
  //   LDA [2]
  //   2
  //   SUB [3]
  //   3
  //   Memoria de instrucciones
  //   ProgramaAC-1.mem
  //    = 0x40 hex
  //    = 0x01 hex
  //    = 0x42 hex
  //    = 0x23 hex
  //   Dirección
  //   CodeOp
  //   AC
  //   AluY
  //   ALUOp
  //   0
  //   1
  //   2
  //   3
  //   DatosAC.mem
  //   0x02 hex
  //   0x03 hex
  //   0x05 hex
  //   0x01 hex
  //   Memoria de datos
endmodule

module Sin_AC_3_Von_Neuman (
  input  Clock
);

  wire AluOp, AluY;
  wire [4:0] adder_1_out, multiplexer_1_out, register_1_q, register_2_q;
  wire [7:0] multiplexer_2_out, ram_1_data, register_3_q, sumador_restador_8_bits_1_resultado;
  wire [7:5] register_2_q_2;

  // Probe on register_1_q
  // Probe on adder_1_out
  Adder #(.width(5)) adder_1 (.a(register_1_q), .b(5'b00001), .out(adder_1_out));  // open: cin, cout
  Register #(.width(5), .trigger("falling")) register_1 (
    .D(adder_1_out), .Q(register_1_q), .clk(Clock));  // open: en, clr
  // Probe on register_1_q
  // Probe on register_1_q
  // Probe on register_2_q
  // Probe on register_2_q
  Multiplexer #(.width(5), .enable("false")) multiplexer_1 (
    .in0(register_1_q), .in1(register_2_q), .out(multiplexer_1_out), .sel(Clock));
  RAM #(.addrWidth(5)) ram_1 (.addr(multiplexer_1_out), .data(ram_1_data));  // open: sel, clk, ld, clr
  Register register_2 (.D(ram_1_data), .Q({register_2_q_2, register_2_q}), .clk(Clock));  // open: en, clr
  // Probe on register_2_q_2
  // Probe on register_2_q_2
  Register #(.trigger("falling")) register_3 (
    .D(sumador_restador_8_bits_1_resultado), .Q(register_3_q), .clk(Clock));  // open: en, clr
  Decoder #(.select(3), .disabled(0), .enable("false")) decoder_1 (
    .out1(AluOp), .out2(AluY), .sel(register_2_q_2));  // open: out0, out3, out4, out5, out6, out7
  // Probe on sumador_restador_8_bits_1_resultado
  // Probe on sumador_restador_8_bits_1_resultado
  // Probe on sumador_restador_8_bits_1_resultado
  Multiplexer #(.width(8), .enable("false")) multiplexer_2 (
    .in0(register_3_q), .in1({8{1'b0}}), .out(multiplexer_2_out), .sel(AluY));
  // Probe on multiplexer_2_out
  // Probe on multiplexer_2_out
  // Probe on multiplexer_2_out
  // Probe on ram_1_data
  // Probe on ram_1_data
  // Probe on ram_1_data
  Sumador_Restador_8_bits sumador_restador_8_bits_1 (
    .Op(AluOp), .A(multiplexer_2_out), .B(ram_1_data), .Resultado(sumador_restador_8_bits_1_resultado));  // open: Acarreo_out

  // Other names for the same wires on the sheet: SelPC_Data = Clock

  // Notes on the sheet:
  //   Sintaxis
  //   ADD [dirección]
  //   SUB [dirección]
  //   LDA [dirección]
  //   Registro PC =
  //   Set de instrucciones
  //   Program Counter
  //   CodeOp
  //   000
  //   0 =
  //   1 =
  //   001
  //   2 =
  //   010
  //    El registro PC y AC se escriben por flanco descendente (Falling edge)
  //    PC + 1
  //   AluY
  //   0
  //   0
  //   1
  //   PC
  //   Sim-AC-3-Von Neumann
  //   ALUOp
  //   0
  //   1
  //   0
  //   Dirección
  //   LDA [4]
  //   0
  //   ADD [5]
  //   1
  //   LDA [6]
  //   2
  //   SUB [7]
  //   3
  //   0x02 hex
  //   4
  //   0x03 hex
  //   5
  //   0x04 hex
  //   6
  //   0x01 hex
  //   7
  //   CodeOp
  //   Memoria de instrucciones y datos
  //   ProgramaAC-VonNeumann.mem
  //    = 0x44 hex
  //    = 0x05 hex
  //    = 0x46 hex
  //    = 0x27 hex
  //   Formato Instrucción
  //   Dirección
  //   | b7 b6  b5 | b4 b3 b2 b1 b0 | 
  //   (byte 1)
  //   IR
  //   CodeOp
  //   AC
  //   Unidad de Control
endmodule

module Sim_AC_4_Harvard (
  input  Clock
);

  wire AluOp, AluX, AluY, decoder_1_out0, WriteR;
  wire [5:0] adder_1_out, register_1_q;
  wire [7:0] multiplexer_1_out, multiplexer_2_out, ram_1_data, ram_2_data, register_2_q,
       sumador_restador_8_bits_1_resultado;

  // Probe on register_1_q
  // Probe on adder_1_out
  Adder #(.width(6)) adder_1 (.a(register_1_q), .b(6'b000001), .out(adder_1_out));  // open: cin, cout
  Register #(.width(6), .trigger("falling")) register_1 (
    .D(adder_1_out), .Q(register_1_q), .clk(Clock));  // open: en, clr
  // Probe on register_1_q
  // Probe on register_1_q
  RAM #(.addrWidth(6)) ram_1 (.addr(register_1_q), .data(ram_1_data));  // open: sel, clk, ld, clr
  // Probe on ram_1_data[4:0]
  // Probe on ram_1_data[4:0]
  // Probe on ram_1_data[7:5]
  // Probe on ram_1_data[7:5]
  Decoder #(.select(3), .enable("false")) decoder_1 (
    .out0(decoder_1_out0), .out1(AluOp), .out2(AluY), .out3(AluX), .sel(ram_1_data[7:5]));  // open: out4, out5, out6, out7
  Register #(.trigger("falling")) register_2 (
    .D(sumador_restador_8_bits_1_resultado), .en(WriteR), .Q(register_2_q), .clk(Clock));  // open: clr
  // Probe on sumador_restador_8_bits_1_resultado
  // Probe on sumador_restador_8_bits_1_resultado
  // Probe on sumador_restador_8_bits_1_resultado
  Multiplexer #(.width(8), .enable("false")) multiplexer_1 (
    .in0(register_2_q), .in1({8{1'b0}}), .out(multiplexer_1_out), .sel(AluY));
  Multiplexer #(.width(8), .enable("false")) multiplexer_2 (
    .in0(ram_2_data), .in1({8{1'b0}}), .out(multiplexer_2_out), .sel(AluX));
  or or_1 (WriteR, decoder_1_out0, AluOp, AluY);
  // Probe on multiplexer_1_out
  // Probe on multiplexer_1_out
  // Probe on multiplexer_1_out
  // Probe on multiplexer_2_out
  // Probe on multiplexer_2_out
  // Probe on multiplexer_2_out
  Sumador_Restador_8_bits sumador_restador_8_bits_1 (
    .Op(AluOp), .A(multiplexer_1_out), .B(multiplexer_2_out), .Resultado(sumador_restador_8_bits_1_resultado));  // open: Acarreo_out
  RAM #(.addrWidth(5), .bus("separate")) ram_2 (
    .addr(ram_1_data[4:0]), .din(sumador_restador_8_bits_1_resultado), .data(ram_2_data), .str(AluX),
    .clk(Clock));  // open: sel, ld, clr

  // Other names for the same wires on the sheet: WriteMD = AluX

  // Notes on the sheet:
  //   Sintaxis
  //   ADD [dirección]
  //   SUB [dirección]
  //   LDA [dirección]
  //   STA [dirección]
  //   CodeOp
  //   0 =
  //   1 =
  //   2 =
  //   3 =
  //   STA [dirección] = STORE ACCUMULATOR
  //   Set de instrucciones
  //   AluY
  //   0
  //   000
  //   0
  //   001
  //   1
  //   010
  //   0
  //   011
  //   Sim-AC-4-Harvard
  //   ALUOp
  //   AluX
  //   0
  //   0
  //   0
  //   0
  //   0
  //   1
  //    PC + 1
  //   WriteR
  //   0
  //   1
  //   1
  //   1
  //   1
  //   0
  //   PC
  //   WriteMD
  //   0
  //   0
  //   0
  //   1
  //   ProgramaAC-2.mem
  //   LDA [0]
  //   0
  //   ADD [1]
  //   1
  //   STA [2]
  //   2
  //   Formato Instrucción
  //   CodeOp
  //   | b7 b6  b5 | b4 b3 b2 b1 b0 | 
  //   Memoria de instrucciones
  //    = 0x40 hex
  //    = 0x01 hex
  //    = 0x62 hex
  //   Dirección
  //   (byte 1)
  //   Dirección
  //   CodeOp
  //   AC
  //   Unidad de Control
  //    Habilitación escritura registro AC
  //    Habilitación escritura Memoria de Datos
  //   La memoria se escibe por flanco ascendente o de subida (Rising edge)
  //   0
  //   1
  //   DatosAC-2.mem
  //   0x02 hex
  //   0x03 hex
  //   Memoria de datos
endmodule

module Sim_AC_4_Von_Neumann (
  input  Clock
);

  wire AluOp, AluY, decoder_1_out0, not_1_out, WriteM, WriteR;
  wire [4:0] adder_1_out, multiplexer_1_out, register_1_q;
  wire [7:0] multiplexer_2_out, ram_1_data, register_2_q, register_3_q, sumador_restador_8_bits_1_resultado;

  // Probe on register_1_q
  // Probe on adder_1_out
  Adder #(.width(5)) adder_1 (.a(register_1_q), .b(5'b00001), .out(adder_1_out));  // open: cin, cout
  Register #(.width(5), .trigger("falling")) register_1 (
    .D(adder_1_out), .Q(register_1_q), .clk(Clock));  // open: en, clr
  // Probe on register_1_q
  // Probe on register_1_q
  // Probe on register_2_q[4:0]
  // Probe on register_2_q[4:0]
  Multiplexer #(.width(5), .enable("false")) multiplexer_1 (
    .in0(register_1_q), .in1(register_2_q[4:0]), .out(multiplexer_1_out), .sel(Clock));
  RAM #(.addrWidth(5), .bus("separate")) ram_1 (
    .addr(multiplexer_1_out), .din(register_3_q), .data(ram_1_data), .str(WriteM), .clk(not_1_out));  // open: sel, ld, clr
  not not_1 (not_1_out, Clock);
  Register register_2 (.D(ram_1_data), .Q(register_2_q), .clk(Clock));  // open: en, clr
  // Probe on register_2_q[7:5]
  // Probe on register_2_q[7:5]
  Decoder #(.select(3), .disabled(0), .enable("false")) decoder_1 (
    .out0(decoder_1_out0), .out1(AluOp), .out2(AluY), .out3(WriteM), .sel(register_2_q[7:5]));  // open: out4, out5, out6, out7
  Register #(.trigger("falling")) register_3 (
    .D(sumador_restador_8_bits_1_resultado), .en(WriteR), .Q(register_3_q), .clk(Clock));  // open: clr
  // Probe on sumador_restador_8_bits_1_resultado
  // Probe on sumador_restador_8_bits_1_resultado
  // Probe on sumador_restador_8_bits_1_resultado
  Multiplexer #(.width(8), .enable("false")) multiplexer_2 (
    .in0(register_3_q), .in1({8{1'b0}}), .out(multiplexer_2_out), .sel(AluY));
  // Probe on multiplexer_2_out
  // Probe on multiplexer_2_out
  // Probe on multiplexer_2_out
  // Probe on ram_1_data
  // Probe on ram_1_data
  // Probe on ram_1_data
  or or_1 (WriteR, decoder_1_out0, AluOp, AluY);
  Sumador_Restador_8_bits sumador_restador_8_bits_1 (
    .Op(AluOp), .A(multiplexer_2_out), .B(ram_1_data), .Resultado(sumador_restador_8_bits_1_resultado));  // open: Acarreo_out

  // Other names for the same wires on the sheet: SelPC_Data = Clock

  // Notes on the sheet:
  //   Sintaxis
  //   Set de instrucciones
  //   ADD [dirección]
  //   SUB [dirección]
  //   LDA [dirección]
  //   STA [dirección]
  //   CodeOp
  //   0 =
  //   1 =
  //   2 =
  //   3 =
  //   STA [dirección] = STORE ACCUMULATOR
  //   LDA [4]
  //   0
  //   ADD [5]
  //   1
  //   STA [6]
  //   2
  //   SUB [7]
  //   3
  //   0x02 hex
  //   4
  //   0x03 hex
  //   5
  //   0x04 hex
  //   6
  //   0x01 hex
  //   7
  //   AluY
  //   0
  //   000
  //   0
  //   001
  //   1
  //   010
  //   0
  //   011
  //    PC + 1
  //   ProgramaAC-VonNeumann.mem
  //    = 0x44 hex
  //    = 0x05 hex
  //    = 0x66 hex
  //    = 0x27 hex
  //   Sim-AC-4-Von Neumann
  //   ALUOp
  //   0
  //   1
  //   0
  //   0
  //   PC
  //   WriteR
  //   WriteM
  //   1
  //   0
  //   0
  //   1
  //   1
  //   0
  //   1
  //   0
  //   Dirección
  //   Formato Instrucción
  //   CodeOp
  //   | b7 b6  b5 | b4 b3 b2 b1 b0 | 
  //   Memoria de instrucciones y datos
  //   La memoria se escibe por flanco ascendente o de subida (Rising edge)
  //   La habilitacion de escritura WriteM se activa cuando el Clock =1
  //   Al negar el Clock la memoria escribe por Flanco descendente
  //   Dirección
  //   (byte 1)
  //   IR
  //   CodeOp
  //   AC
  //   Unidad de Control
  //    Habilitación escritura registro AC
  //    Habilitación escritura en memoria
endmodule

module Sim_AC_5_Harvard (
  input  Clock
);

  wire AluOp, AluX, AluY, decoder_1_out0, WriteR;
  wire [5:0] counter_1_q;
  wire [7:0] multiplexer_1_out, multiplexer_2_out, ram_1_data, ram_2_data, register_1_q,
       sumador_restador_8_bits_1_resultado;

  Counter #(.width(6), .max('h3f), .trigger("falling")) counter_1 (
    .Q(counter_1_q), .clk(Clock));  // open: load, D, count, carry, clr
  // Probe on counter_1_q
  // Probe on counter_1_q
  RAM #(.addrWidth(6)) ram_1 (.addr(counter_1_q), .data(ram_1_data));  // open: sel, clk, ld, clr
  // Probe on ram_1_data[4:0]
  // Probe on ram_1_data[4:0]
  // Probe on ram_1_data[7:5]
  // Probe on ram_1_data[7:5]
  Decoder #(.select(3), .enable("false")) decoder_1 (
    .out0(decoder_1_out0), .out1(AluOp), .out2(AluY), .out3(AluX), .sel(ram_1_data[7:5]));  // open: out4, out5, out6, out7
  Register register_1 (
    .D(sumador_restador_8_bits_1_resultado), .en(WriteR), .Q(register_1_q), .clk(Clock));  // open: clr
  or or_1 (WriteR, decoder_1_out0, AluOp, AluY);
  // Probe on sumador_restador_8_bits_1_resultado
  // Probe on sumador_restador_8_bits_1_resultado
  // Probe on sumador_restador_8_bits_1_resultado
  Multiplexer #(.width(8), .enable("false")) multiplexer_1 (
    .in0(register_1_q), .in1({8{1'b0}}), .out(multiplexer_1_out), .sel(AluY));
  Multiplexer #(.width(8), .enable("false")) multiplexer_2 (
    .in0(ram_2_data), .in1({8{1'b0}}), .out(multiplexer_2_out), .sel(AluX));
  // Probe on multiplexer_1_out
  // Probe on multiplexer_1_out
  // Probe on multiplexer_1_out
  // Probe on multiplexer_2_out
  // Probe on multiplexer_2_out
  // Probe on multiplexer_2_out
  Sumador_Restador_8_bits sumador_restador_8_bits_1 (
    .Op(AluOp), .A(multiplexer_1_out), .B(multiplexer_2_out), .Resultado(sumador_restador_8_bits_1_resultado));  // open: Acarreo_out
  RAM #(.addrWidth(5), .bus("separate")) ram_2 (
    .addr(ram_1_data[4:0]), .din(sumador_restador_8_bits_1_resultado), .data(ram_2_data), .str(AluX),
    .clk(Clock));  // open: sel, ld, clr

  // Other names for the same wires on the sheet: WriteMD = AluX

  // Notes on the sheet:
  //   Tipo
  //   Procesamiento de datos
  //   Transferencia
  //   PC
  //   PC =  PC + 1
  //   Set de instrucciones
  //   Sintaxis
  //   ADD [dirección]
  //   SUB [dirección]
  //   LDA [dirección]
  //   STA [dirección]
  //   ProgramaAC-2.mem
  //   LDA [0]
  //   0
  //   ADD [1]
  //   1
  //   STA [2]
  //   2
  //   Sim-AC-5-Harvard
  //   Memoria de instrucciones
  //    = 0x40 hex
  //    = 0x01 hex
  //    = 0x62 hex
  //   !!Se organiza las instrucciones por tipo
  //   CodeOp
  //   000
  //   0 =
  //   1 =
  //   001
  //   2 =
  //   010
  //   3 =
  //   011
  //   CodeOp
  //   AluY
  //   AluX
  //   0
  //   0
  //   0
  //   0
  //   1
  //   0
  //   0
  //   1
  //   Dirección
  //   ALUOp
  //   0
  //   1
  //   0
  //   0
  //   AC
  //   WriteMD
  //   WriteR
  //   1
  //   0
  //   1
  //   0
  //   1
  //   0
  //   0
  //   1
  //   Unidad de Control
  //   CodeOp
  //   Formato Instrucción
  //   Dirección
  //   | b7 b6  b5 | b4 b3 b2 b1 b0 | 
  //   (byte 1)
  //   DatosAC-2.mem
  //   0
  //   1
  //   Memoria de datos
  //   0x02 hex
  //   0x03 hex
endmodule

module Sim_AC_5_Von_Neumann (
  input  Clock
);

  wire AluOp, AluY, decoder_1_out0, not_1_out, WriteM, WriteR;
  wire [4:0] counter_1_q, multiplexer_1_out, register_1_q;
  wire [7:0] multiplexer_2_out, ram_1_data, register_2_q, sumador_restador_8_bits_1_resultado;
  wire [7:5] register_1_q_2;

  Counter #(.width(5), .max('h1f), .trigger("falling")) counter_1 (
    .Q(counter_1_q), .clk(Clock));  // open: load, D, count, carry, clr
  // Probe on counter_1_q
  // Probe on counter_1_q
  // Probe on register_1_q
  // Probe on register_1_q
  Multiplexer #(.width(5), .enable("false")) multiplexer_1 (
    .in0(counter_1_q), .in1(register_1_q), .out(multiplexer_1_out), .sel(Clock));
  not not_1 (not_1_out, Clock);
  RAM #(.addrWidth(5), .bus("separate")) ram_1 (
    .addr(multiplexer_1_out), .din(register_2_q), .data(ram_1_data), .str(WriteM), .clk(not_1_out));  // open: sel, ld, clr
  Register register_1 (.D(ram_1_data), .Q({register_1_q_2, register_1_q}), .clk(Clock));  // open: en, clr
  // Probe on register_1_q_2
  // Probe on register_1_q_2
  Decoder #(.select(3), .disabled(0), .enable("false")) decoder_1 (
    .out0(decoder_1_out0), .out1(AluOp), .out2(AluY), .out3(WriteM), .sel(register_1_q_2));  // open: out4, out5, out6, out7
  Register #(.trigger("falling")) register_2 (
    .D(sumador_restador_8_bits_1_resultado), .en(WriteR), .Q(register_2_q), .clk(Clock));  // open: clr
  // Probe on sumador_restador_8_bits_1_resultado
  // Probe on sumador_restador_8_bits_1_resultado
  // Probe on sumador_restador_8_bits_1_resultado
  Multiplexer #(.width(8), .enable("false")) multiplexer_2 (
    .in0(register_2_q), .in1({8{1'b0}}), .out(multiplexer_2_out), .sel(AluY));
  or or_1 (WriteR, decoder_1_out0, AluOp, AluY);
  // Probe on multiplexer_2_out
  // Probe on multiplexer_2_out
  // Probe on multiplexer_2_out
  // Probe on ram_1_data
  // Probe on ram_1_data
  // Probe on ram_1_data
  Sumador_Restador_8_bits sumador_restador_8_bits_1 (
    .Op(AluOp), .A(multiplexer_2_out), .B(ram_1_data), .Resultado(sumador_restador_8_bits_1_resultado));  // open: Acarreo_out

  // Other names for the same wires on the sheet: SelPC_Data = Clock

  // Notes on the sheet:
  //   Tipo
  //   Procesamiento de datos
  //   Transferencia
  //   Set de instrucciones
  //   PC
  //   PC =  PC + 1
  //   Sintaxis
  //   ADD [dirección]
  //   SUB [dirección]
  //   LDA [dirección]
  //   STA [dirección]
  //   Dirección
  //   Sim-AC-5-Von Neumann
  //   0
  //   1
  //   2
  //   3
  //   4
  //   5
  //   6
  //   7
  //   !!Se organiza las instrucciones por tipo
  //   CodeOp
  //   000
  //   0 =
  //   1 =
  //   001
  //   2 =
  //   010
  //   3 =
  //   011
  //   Memoria de instrucciones y datos
  //   ProgramaAC-VonNeumann.mem
  //   LDA [4]
  //   ADD [5]
  //   STA [6]
  //   SUB [7]
  //   0x02 hex
  //   0x03 hex
  //   0x04 hex
  //   0x01 hex
  //   AluY
  //   ALUOp
  //   0
  //   0
  //   1
  //   0
  //   0
  //   0
  //    = 0x44 hex
  //    = 0x05 hex
  //    = 0x66 hex
  //    = 0x27 hex
  //   WriteR
  //   0
  //   1
  //   1
  //   1
  //   1
  //   0
  //   IR
  //   WriteMD
  //   0
  //   0
  //   0
  //   1
  //   CodeOp
  //   CodeOp
  //   AC
  //   Formato Instrucción
  //   Dirección
  //   | b7 b6  b5 | b4 b3 b2 b1 b0 | 
  //   Unidad de Control
  //   (byte 1)
  //    Habilitación escritura registro AC
  //    Habilitación escritura en memoria
endmodule

module Sim_AC_6_Harvard (
  input  Clock
);

  wire AluOp, AluX, AluY, decoder_1_out0, JMP, not_1_out, WriteR;
  wire [4:0] counter_1_q;
  wire [7:0] multiplexer_1_out, multiplexer_2_out, ram_1_data, ram_2_data, register_1_q,
       sumador_restador_8_bits_1_resultado;

  not not_1 (not_1_out, JMP);
  Counter #(.width(5), .max('h1f), .trigger("falling")) counter_1 (
    .load(JMP), .D(ram_1_data[4:0]), .count(not_1_out), .Q(counter_1_q), .clk(Clock));  // open: carry, clr
  // Probe on counter_1_q
  // Probe on counter_1_q
  RAM #(.addrWidth(5)) ram_1 (.addr(counter_1_q), .data(ram_1_data));  // open: sel, clk, ld, clr
  // Probe on ram_1_data[4:0]
  // Probe on ram_1_data[4:0]
  // Probe on ram_1_data[7:5]
  // Probe on ram_1_data[7:5]
  Decoder #(.select(3), .enable("false")) decoder_1 (
    .out0(decoder_1_out0), .out1(AluOp), .out2(AluY), .out3(AluX), .out4(JMP), .sel(ram_1_data[7:5]));  // open: out5, out6, out7
  Register register_1 (
    .D(sumador_restador_8_bits_1_resultado), .en(WriteR), .Q(register_1_q), .clk(Clock));  // open: clr
  Multiplexer #(.width(8), .enable("false")) multiplexer_1 (
    .in0(register_1_q), .in1({8{1'b0}}), .out(multiplexer_1_out), .sel(AluY));
  Multiplexer #(.width(8), .enable("false")) multiplexer_2 (
    .in0(ram_2_data), .in1({8{1'b0}}), .out(multiplexer_2_out), .sel(AluX));
  or or_1 (WriteR, decoder_1_out0, AluOp, AluY);
  // Probe on multiplexer_1_out
  // Probe on multiplexer_1_out
  // Probe on multiplexer_1_out
  // Probe on multiplexer_2_out
  // Probe on multiplexer_2_out
  // Probe on multiplexer_2_out
  // Probe on sumador_restador_8_bits_1_resultado
  // Probe on sumador_restador_8_bits_1_resultado
  // Probe on sumador_restador_8_bits_1_resultado
  Sumador_Restador_8_bits sumador_restador_8_bits_1 (
    .Op(AluOp), .A(multiplexer_1_out), .B(multiplexer_2_out), .Resultado(sumador_restador_8_bits_1_resultado));  // open: Acarreo_out
  RAM #(.addrWidth(5), .bus("separate")) ram_2 (
    .addr(ram_1_data[4:0]), .din(sumador_restador_8_bits_1_resultado), .data(ram_2_data), .str(AluX),
    .clk(Clock));  // open: sel, ld, clr

  // Other names for the same wires on the sheet: WriteMD = AluX

  // Notes on the sheet:
  //   Tipo
  //   Procesamiento de datos
  //   Transferencia
  //   Control de flujo
  //   Set de instrucciones
  //   Load
  //   PC =  PC + 1
  //   Sintaxis
  //   ADD [Dirección]
  //   SUB [Dirección]
  //   LDA [Dirección]
  //   STA [Dirección]
  //   JMP Dirección
  //   PC
  //   Sim-AC-6-Harvard
  //   En las instrucciones de control de flujo la [dirección] es una posición de la memoria de instrucciones
  //   0
  //   1
  //   2
  //   3
  //   CodeOp
  //   000
  //   0 =
  //   001
  //   1 =
  //   2 =
  //   010
  //   3 =
  //   011
  //   4 =
  //   100
  //   Memoria de instrucciones
  //   ProgramaAC-3.mem
  //   LDA [0]
  //   JMP [3]
  //   STA [2]
  //   JMP 0
  //   AluY
  //   0
  //   0
  //   1
  //   0
  //   0
  //    = 0x40 hex
  //    = 0x83 hex
  //    = 0x62 hex
  //    = 0x80 hex
  //   ALUOp
  //   AluX
  //   0
  //   0
  //   0
  //   1
  //   0
  //   0
  //   1
  //   0
  //   0
  //   0
  //   Dirección
  //   CodeOp
  //   WriteMD
  //   WriteR
  //   1
  //   0
  //   1
  //   0
  //   1
  //   0
  //   0
  //   1
  //   0
  //   0
  //   JMP
  //   0
  //   0
  //   0
  //   1
  //   1
  //   AC
  //   Unidad de Control
  //   Formato Instrucción
  //   CodeOp
  //   Dirección
  //   | b7 b6 b5 | b4 b3 b2 b1 b0 | 
  //   (byte 1)
  //   0x02 hex
  //   0
  //   0x03 hex
  //   1
  //   Memoria de datos
  //   DatosAC-3.mem
endmodule

module Sim_AC_6_Von_Neumann (
  input  Clock
);

  wire AluOp, AluY, decoder_1_out0, JMP, not_1_out, not_2_out, WriteM, WriteR;
  wire [4:0] counter_1_q, multiplexer_1_out, register_1_q;
  wire [7:0] multiplexer_2_out, ram_1_data, register_2_q, sumador_restador_8_bits_1_resultado;
  wire [7:5] register_1_q_2;

  not not_1 (not_1_out, JMP);
  // Probe on counter_1_q
  // Probe on counter_1_q
  Counter #(.width(5), .max('h1f), .trigger("falling")) counter_1 (
    .load(JMP), .D(register_1_q), .count(not_1_out), .Q(counter_1_q), .clk(Clock));  // open: carry, clr
  // Probe on register_1_q
  // Probe on register_1_q
  Multiplexer #(.width(5), .enable("false")) multiplexer_1 (
    .in0(counter_1_q), .in1(register_1_q), .out(multiplexer_1_out), .sel(Clock));
  not not_2 (not_2_out, Clock);
  RAM #(.addrWidth(5), .bus("separate")) ram_1 (
    .addr(multiplexer_1_out), .din(register_2_q), .data(ram_1_data), .str(WriteM), .clk(not_2_out));  // open: sel, ld, clr
  Register register_1 (.D(ram_1_data), .Q({register_1_q_2, register_1_q}), .clk(Clock));  // open: en, clr
  Register #(.trigger("falling")) register_2 (
    .D(sumador_restador_8_bits_1_resultado), .en(WriteR), .Q(register_2_q), .clk(Clock));  // open: clr
  // Probe on register_1_q_2
  // Probe on register_1_q_2
  Decoder #(.select(3), .disabled(0), .enable("false")) decoder_1 (
    .out0(decoder_1_out0), .out1(AluOp), .out2(AluY), .out3(WriteM), .out4(JMP), .sel(register_1_q_2));  // open: out5, out6, out7
  // Probe on sumador_restador_8_bits_1_resultado
  // Probe on sumador_restador_8_bits_1_resultado
  // Probe on sumador_restador_8_bits_1_resultado
  // Probe on multiplexer_2_out
  Multiplexer #(.width(8), .enable("false")) multiplexer_2 (
    .in0(register_2_q), .in1({8{1'b0}}), .out(multiplexer_2_out), .sel(AluY));
  // Probe on multiplexer_2_out
  // Probe on multiplexer_2_out
  // Probe on ram_1_data
  // Probe on ram_1_data
  // Probe on ram_1_data
  or or_1 (WriteR, decoder_1_out0, AluOp, AluY);
  Sumador_Restador_8_bits sumador_restador_8_bits_1 (
    .Op(AluOp), .A(multiplexer_2_out), .B(ram_1_data), .Resultado(sumador_restador_8_bits_1_resultado));  // open: Acarreo_out

  // Other names for the same wires on the sheet: SelPC_Data = Clock

  // Notes on the sheet:
  //   Tipo
  //   Procesamiento de datos
  //   Transferencia
  //   Control de flujo
  //   0
  //   1
  //   2
  //   3
  //   4
  //   Set de instrucciones
  //   Load
  //    = 0x44 hex
  //   LDA [4]
  //   JMP [3]
  //    = 0x83 hex
  //   STA [5]
  //    = 0x65 hex
  //   JMP 0
  //    = 0x80 hex
  //   0x02 hex
  //   Sintaxis
  //   ADD [Dirección]
  //   SUB [Dirección]
  //   LDA [Dirección]
  //   STA [Dirección]
  //   JMP Dirección
  //   PC
  //   PC =  PC + 1
  //   ProgramaAC-VonNeumann.mem
  //   Sim-AC-6-Von Neumann
  //   CodeOp
  //   000
  //   0 =
  //   001
  //   1 =
  //   2 =
  //   010
  //   3 =
  //   011
  //   4 =
  //   100
  //   Dirección
  //   AluY
  //   0
  //   0
  //   1
  //   0
  //   0
  //   ALUOp
  //   AluX
  //   0
  //   0
  //   1
  //   0
  //   0
  //   0
  //   1
  //   0
  //   0
  //   0
  //   Memoria de instrucciones y datos
  //   WriteR
  //   WriteMD
  //   1
  //   0
  //   1
  //   0
  //   1
  //   0
  //   0
  //   1
  //   0
  //   0
  //   JMP
  //   0
  //   0
  //   0
  //   1
  //   1
  //   IR
  //   Formato Instrucción
  //   CodeOp
  //   AC
  //   CodeOp
  //   Dirección
  //   | b7 b6 b5 | b4 b3 b2 b1 b0 | 
  //   (byte 1)
  //   Unidad de Control
  //    Habilitación escritura registro AC
  //    Habilitación escritura en memoria
endmodule

module Sim_AC_7_Harvard (
  input  Clock
);

  wire AluOp, AluX, AluY, and_1_out, decoder_1_out0, decoder_1_out4, decoder_1_out5, FZ, JMP, not_1_out,
       WriteF, WriteR, Z;
  wire [4:0] counter_1_q;
  wire [7:0] multiplexer_1_out, multiplexer_2_out, ram_1_data, ram_2_data, register_2_q,
       sumador_restador_con_flags_1_resultado;

  not not_1 (not_1_out, JMP);
  Counter #(.width(5), .max('h1f), .trigger("falling")) counter_1 (
    .load(JMP), .D(ram_1_data[4:0]), .count(not_1_out), .Q(counter_1_q), .clk(Clock));  // open: carry, clr
  // Probe on counter_1_q
  // Probe on counter_1_q
  RAM #(.addrWidth(5)) ram_1 (.addr(counter_1_q), .data(ram_1_data));  // open: sel, clk, ld, clr
  // Probe on ram_1_data[4:0]
  // Probe on ram_1_data[4:0]
  // Probe on ram_1_data[7:5]
  // Probe on ram_1_data[7:5]
  Register #(.width(1)) register_1 (.D(Z), .en(WriteF), .Q(FZ), .clk(Clock));  // open: clr
  Decoder #(.select(3), .enable("false")) decoder_1 (
    .out0(decoder_1_out0), .out1(AluOp), .out2(AluY), .out3(AluX), .out4(decoder_1_out4),
    .out5(decoder_1_out5), .sel(ram_1_data[7:5]));  // open: out6, out7
  Register register_2 (
    .D(sumador_restador_con_flags_1_resultado), .en(WriteR), .Q(register_2_q), .clk(Clock));  // open: clr
  Multiplexer #(.width(8), .enable("false")) multiplexer_1 (
    .in0(register_2_q), .in1({8{1'b0}}), .out(multiplexer_1_out), .sel(AluY));
  Multiplexer #(.width(8), .enable("false")) multiplexer_2 (
    .in0(ram_2_data), .in1({8{1'b0}}), .out(multiplexer_2_out), .sel(AluX));
  or or_1 (WriteR, decoder_1_out0, AluOp, AluY);
  or or_2 (JMP, decoder_1_out4, and_1_out);
  and and_1 (and_1_out, decoder_1_out5, FZ);
  // Probe on multiplexer_1_out
  // Probe on multiplexer_1_out
  // Probe on multiplexer_1_out
  // Probe on multiplexer_2_out
  // Probe on multiplexer_2_out
  // Probe on multiplexer_2_out
  or or_3 (WriteF, decoder_1_out0, AluOp);
  // Probe on sumador_restador_con_flags_1_resultado
  // Probe on sumador_restador_con_flags_1_resultado
  // Probe on sumador_restador_con_flags_1_resultado
  Sumador_Restador_con_flags sumador_restador_con_flags_1 (
    .Op(AluOp), .A(multiplexer_1_out), .B(multiplexer_2_out), .Cero__Zero(Z),
    .Resultado(sumador_restador_con_flags_1_resultado));  // open: Acarreo__Carry
  RAM #(.addrWidth(5), .bus("separate")) ram_2 (
    .addr(ram_1_data[4:0]), .din(sumador_restador_con_flags_1_resultado), .data(ram_2_data), .str(AluX),
    .clk(Clock));  // open: sel, ld, clr

  // Other names for the same wires on the sheet: WriteMD = AluX

  // Notes on the sheet:
  //   Tipo
  //   Procesamiento de datos
  //   Transferencia
  //   Control de flujo
  //   Set de instrucciones
  //   Load
  //   PC =  PC + 1
  //   Sintaxis
  //   ADD [dirección]
  //   SUB [dirección]
  //   LDA [dirección]
  //   STA [dirección]
  //   JMP Dirección
  //   JZ     Dirección
  //   La instrucción JZ salta si el registro Z tiene valor 1
  //   PC
  //   0
  //   1
  //   2
  //   3
  //   Sim-AC-7-Harvard
  //   CodeOp
  //   000
  //   0 =
  //   001
  //   1 =
  //   2 =
  //   010
  //   3 =
  //   011
  //   4 =
  //   100
  //   5 =
  //   101
  //   Memoria de instrucciones
  //   ProgramaAC-4.mem
  //   LDA [0]
  //   SUB [1]
  //   JZ 0
  //   JMP 0
  //   AluY
  //   0
  //   0
  //   1
  //   0
  //   0
  //   0
  //    = 0x40 hex
  //    = 0x21 hex
  //    = 0xA0 hex
  //    = 0x80 hex
  //   ALUOp
  //   AluX
  //   0
  //   0
  //   0
  //   1
  //   0
  //   0
  //   1
  //   0
  //   0
  //   0
  //   0
  //   0
  //   Z
  //   Dirección
  //   CodeOp
  //   WriteMD
  //   WriteR
  //   1
  //   0
  //   1
  //   0
  //   1
  //   0
  //   0
  //   1
  //   0
  //   0
  //   0
  //   0
  //   El registro Z se escibe por flanco ascendente o de subida (Rising edge)
  //   JMP
  //   0
  //   0
  //   0
  //   1
  //   1
  //   1
  //   WriteF
  //   1
  //   1
  //   0
  //   0
  //   0
  //   0
  //   AC
  //   Unidad de Control
  //   Formato Instrucción
  //   CodeOp
  //   Dirección
  //   | b7 b6 b5 | b4 b3 b2 b1 b0 | 
  //   Solo para las instrucciones de procesamiento de datos se escribe los registros Flags
  //   (byte 1)
  //   0x02 hex
  //   0
  //   0x02 hex
  //   1
  //   Memoria de datos
  //   DatosAC-4.mem
endmodule

module Sim_AC_7_Von_Neumann (
  input  Clock
);

  wire AluOp, AluY, and_1_out, decoder_1_out0, decoder_1_out4, decoder_1_out5, FZ, JMP, not_1_out, not_2_out,
       WriteF, WriteM, WriteR, Z;
  wire [4:0] counter_1_q, multiplexer_1_out;
  wire [7:0] multiplexer_2_out, ram_1_data, register_2_q, register_3_q,
       sumador_restador_con_flags_1_resultado;

  not not_1 (not_1_out, JMP);
  Counter #(.width(5), .max('h1f), .trigger("falling")) counter_1 (
    .load(JMP), .D(register_2_q[4:0]), .count(not_1_out), .Q(counter_1_q), .clk(Clock));  // open: carry, clr
  // Probe on counter_1_q
  // Probe on counter_1_q
  // Probe on register_2_q[4:0]
  // Probe on register_2_q[4:0]
  Multiplexer #(.width(5), .enable("false")) multiplexer_1 (
    .in0(counter_1_q), .in1(register_2_q[4:0]), .out(multiplexer_1_out), .sel(Clock));
  not not_2 (not_2_out, Clock);
  RAM #(.addrWidth(5), .bus("separate")) ram_1 (
    .addr(multiplexer_1_out), .din(register_3_q), .data(ram_1_data), .str(WriteM), .clk(not_2_out));  // open: sel, ld, clr
  Register #(.width(1), .trigger("falling")) register_1 (.D(Z), .en(WriteF), .Q(FZ), .clk(Clock));  // open: clr
  Register register_2 (.D(ram_1_data), .Q(register_2_q), .clk(Clock));  // open: en, clr
  // Probe on register_2_q[7:5]
  // Probe on register_2_q[7:5]
  Register #(.trigger("falling")) register_3 (
    .D(sumador_restador_con_flags_1_resultado), .en(WriteR), .Q(register_3_q), .clk(Clock));  // open: clr
  Decoder #(.select(3), .disabled(0), .enable("false")) decoder_1 (
    .out0(decoder_1_out0), .out1(AluOp), .out2(AluY), .out3(WriteM), .out4(decoder_1_out4),
    .out5(decoder_1_out5), .sel(register_2_q[7:5]));  // open: out6, out7
  Multiplexer #(.width(8), .enable("false")) multiplexer_2 (
    .in0(register_3_q), .in1({8{1'b0}}), .out(multiplexer_2_out), .sel(AluY));
  // Probe on multiplexer_2_out
  // Probe on multiplexer_2_out
  // Probe on multiplexer_2_out
  // Probe on ram_1_data
  // Probe on ram_1_data
  // Probe on ram_1_data
  or or_1 (WriteF, decoder_1_out0, AluOp);
  or or_2 (WriteR, decoder_1_out0, AluOp, AluY);
  or or_3 (JMP, decoder_1_out4, and_1_out);
  and and_1 (and_1_out, decoder_1_out5, FZ);
  // Probe on sumador_restador_con_flags_1_resultado
  // Probe on sumador_restador_con_flags_1_resultado
  // Probe on sumador_restador_con_flags_1_resultado
  Sumador_Restador_con_flags sumador_restador_con_flags_1 (
    .Op(AluOp), .A(multiplexer_2_out), .B(ram_1_data), .Cero__Zero(Z),
    .Resultado(sumador_restador_con_flags_1_resultado));  // open: Acarreo__Carry

  // Other names for the same wires on the sheet: SelPC_Data = Clock

  // Notes on the sheet:
  //   Tipo
  //   Procesamiento de datos
  //   Transferencia
  //   Control de flujo
  //   Load
  //   Set de instrucciones
  //   PC
  //   PC =  PC + 1
  //   Sintaxis
  //   ADD [dirección]
  //   SUB [dirección]
  //   LDA [dirección]
  //   STA [dirección]
  //   JMP Dirección
  //   JZ    Dirección
  //   La instrucción JZ salta si el registro Z tiene valor 1
  //   Dirección
  //   LDA [4]
  //   0
  //   1
  //   JZ 0
  //   2
  //   JMP 0
  //   3
  //   4
  //   5
  //   Sim-AC-7-Von Neumann
  //   CodeOp
  //   000
  //   0 =
  //   001
  //   1 =
  //   2 =
  //   010
  //   3 =
  //   011
  //   4 =
  //   100
  //   5 =
  //   101
  //    = 0x44 hex
  //   SUB [5]
  //    = 0x25 hex
  //    = 0xA0 hex
  //    = 0x80 hex
  //   0x02 hex
  //   0x03 hex
  //   AluY
  //   0
  //   0
  //   1
  //   0
  //   0
  //   0
  //   Memoria de instrucciones y datos
  //   ProgramaAC-VonNeumann.mem
  //   WriteR
  //   ALUOp
  //   0
  //   1
  //   1
  //   1
  //   0
  //   1
  //   0
  //   0
  //   0
  //   0
  //   0
  //   0
  //    El registro Z se escribe por flanco descendente o de bajada (Falling edge)
  //   WriteM
  //   0
  //   0
  //   0
  //   1
  //   0
  //   0
  //   Z
  //   IR
  //   JMP
  //   WriteF
  //   1
  //   0
  //   1
  //   0
  //   0
  //   0
  //   0
  //   1
  //   0
  //   1
  //   0
  //   1
  //   CodeOp
  //   AC
  //   CodeOp
  //   Unidad de Control
  //   Formato Instrucción
  //   Dirección
  //   | b7 b6 b5 | b4 b3 b2 b1 b0 | 
  //   (byte 1)
  //   Solo para las instrucciones de procesamiento de datos se escribe los registros Flags
  //    Habilitación escritura registro AC
  //    Habilitación escritura en memoria
endmodule

module Sim_AC_8_Harvard (
  input  Clock
);

  wire AluOp, AluX, AluY, and_1_out, and_2_out, C, decoder_1_out0, decoder_1_out4, decoder_1_out5,
       decoder_1_out6, FC, FZ, JMP, not_1_out, WriteF, WriteR, Z;
  wire [4:0] counter_1_q;
  wire [7:0] multiplexer_1_out, multiplexer_2_out, ram_1_data, ram_2_data, register_3_q,
       sumador_restador_con_flags_1_resultado;

  not not_1 (not_1_out, JMP);
  Counter #(.width(5), .max('h1f), .trigger("falling")) counter_1 (
    .load(JMP), .D(ram_1_data[4:0]), .count(not_1_out), .Q(counter_1_q), .clk(Clock));  // open: carry, clr
  // Probe on counter_1_q
  // Probe on counter_1_q
  Register #(.width(1)) register_1 (.D(Z), .en(WriteF), .Q(FZ), .clk(Clock));  // open: clr
  RAM #(.addrWidth(5)) ram_1 (.addr(counter_1_q), .data(ram_1_data));  // open: sel, clk, ld, clr
  // Probe on ram_1_data[4:0]
  // Probe on ram_1_data[4:0]
  // Probe on ram_1_data[7:5]
  // Probe on ram_1_data[7:5]
  Register #(.width(1)) register_2 (.D(C), .en(WriteF), .Q(FC), .clk(Clock));  // open: clr
  Decoder #(.select(3), .enable("false")) decoder_1 (
    .out0(decoder_1_out0), .out1(AluOp), .out2(AluY), .out3(AluX), .out4(decoder_1_out4),
    .out5(decoder_1_out5), .out6(decoder_1_out6), .sel(ram_1_data[7:5]));  // open: out7
  Register register_3 (
    .D(sumador_restador_con_flags_1_resultado), .en(WriteR), .Q(register_3_q), .clk(Clock));  // open: clr
  Multiplexer #(.width(8), .enable("false")) multiplexer_1 (
    .in0(register_3_q), .in1({8{1'b0}}), .out(multiplexer_1_out), .sel(AluY));
  Multiplexer #(.width(8), .enable("false")) multiplexer_2 (
    .in0(ram_2_data), .in1({8{1'b0}}), .out(multiplexer_2_out), .sel(AluX));
  or or_1 (WriteR, decoder_1_out0, AluOp, AluY);
  and and_1 (and_1_out, decoder_1_out5, FZ);
  and and_2 (and_2_out, decoder_1_out6, FC);
  // Probe on multiplexer_1_out
  // Probe on multiplexer_1_out
  // Probe on multiplexer_1_out
  // Probe on multiplexer_2_out
  // Probe on multiplexer_2_out
  // Probe on multiplexer_2_out
  or or_2 (WriteF, decoder_1_out0, AluOp);
  or or_3 (JMP, decoder_1_out4, and_1_out, and_2_out);
  // Probe on sumador_restador_con_flags_1_resultado
  // Probe on sumador_restador_con_flags_1_resultado
  // Probe on sumador_restador_con_flags_1_resultado
  Sumador_Restador_con_flags sumador_restador_con_flags_1 (
    .Op(AluOp), .A(multiplexer_1_out), .B(multiplexer_2_out), .Acarreo__Carry(C), .Cero__Zero(Z),
    .Resultado(sumador_restador_con_flags_1_resultado));
  RAM #(.addrWidth(5), .bus("separate")) ram_2 (
    .addr(ram_1_data[4:0]), .din(sumador_restador_con_flags_1_resultado), .data(ram_2_data), .str(AluX),
    .clk(Clock));  // open: sel, ld, clr

  // Other names for the same wires on the sheet: WriteMD = AluX

  // Notes on the sheet:
  //   Tipo
  //   Procesamiento de datos
  //   Transferencia
  //   Control de flujo
  //   Set de instrucciones
  //   Load
  //   PC =  PC + 1
  //   Sintaxis
  //   ADD [dirección]
  //   SUB [dirección]
  //   LDA [dirección]
  //   STA [dirección]
  //   JMP Dirección
  //   JZ     Dirección
  //   JC    Dirección
  //   La instrucción JC salta si el registro C tiene valor 1 
  //   PC
  //   0
  //   1
  //   2
  //   3
  //   Sim-AC-8-Harvard
  //   CodeOp
  //   000
  //   0 =
  //   001
  //   1 =
  //   2 =
  //   010
  //   3 =
  //   011
  //   4 =
  //   100
  //   5 =
  //   101
  //   6 =
  //   110
  //   Memoria de instrucciones
  //   ProgramaAC-4.mem
  //   LDA [0]
  //   SUB [1]
  //   JZ  0
  //   JMP 0
  //   AluY
  //   0
  //   0
  //   1
  //   0
  //   0
  //   0
  //   0
  //   Z
  //    = 0x40 hex
  //    = 0x21 hex
  //    = 0xA0 hex
  //    = 0x80 hex
  //   ALUOp
  //   AluX
  //   0
  //   0
  //   1
  //   0
  //   0
  //   0
  //   1
  //   0
  //   0
  //   0
  //   0
  //   0
  //   0
  //   0
  //   C
  //   Dirección
  //   CodeOp
  //   WriteMD
  //   WriteR
  //   1
  //   0
  //   1
  //   0
  //   1
  //   0
  //   0
  //   1
  //   0
  //   0
  //   0
  //   0
  //   0
  //   0
  //   JMP
  //   0
  //   0
  //   0
  //   1
  //   1
  //   1
  //   1
  //   WriteF
  //   1
  //   1
  //   0
  //   0
  //   0
  //   0
  //   0
  //   AC
  //   Unidad de Control
  //   Formato Instrucción
  //   CodeOp
  //   | b7 b6 b5 | b4 b3 b2 b1 b0 | 
  //   (byte 1)
  //   Dirección
  //   0x02 hex
  //   0
  //   0x02 hex
  //   1
  //   Memoria de datos
  //   DatosAC-4.mem
endmodule

module Sim_AC_8_Von_Neumann (
  input  Clock
);

  wire AluOp, AluY, and_1_out, and_2_out, C, decoder_1_out0, decoder_1_out4, decoder_1_out5, decoder_1_out6,
       FC, FZ, JMP, not_1_out, not_2_out, WriteF, WriteM, WriteR, Z;
  wire [4:0] counter_1_q, multiplexer_1_out, register_3_q;
  wire [7:0] multiplexer_2_out, ram_1_data, register_4_q, sumador_restador_con_flags_1_resultado;
  wire [7:5] register_3_q_2;

  not not_1 (not_1_out, JMP);
  Counter #(.width(5), .max('h1f), .trigger("falling")) counter_1 (
    .load(JMP), .D(register_3_q), .count(not_1_out), .Q(counter_1_q), .clk(Clock));  // open: carry, clr
  // Probe on counter_1_q
  // Probe on counter_1_q
  // Probe on register_3_q
  // Probe on register_3_q
  Multiplexer #(.width(5), .enable("false")) multiplexer_1 (
    .in0(counter_1_q), .in1(register_3_q), .out(multiplexer_1_out), .sel(Clock));
  not not_2 (not_2_out, Clock);
  Register #(.width(1), .trigger("falling")) register_1 (.D(Z), .en(WriteF), .Q(FZ), .clk(Clock));  // open: clr
  RAM #(.addrWidth(5), .bus("separate")) ram_1 (
    .addr(multiplexer_1_out), .din(register_4_q), .data(ram_1_data), .str(WriteM), .clk(not_2_out));  // open: sel, ld, clr
  Register #(.width(1), .trigger("falling")) register_2 (.D(C), .en(WriteF), .Q(FC), .clk(Clock));  // open: clr
  Register register_3 (.D(ram_1_data), .Q({register_3_q_2, register_3_q}), .clk(Clock));  // open: en, clr
  // Probe on register_3_q_2
  // Probe on register_3_q_2
  Register #(.trigger("falling")) register_4 (
    .D(sumador_restador_con_flags_1_resultado), .en(WriteR), .Q(register_4_q), .clk(Clock));  // open: clr
  Decoder #(.select(3), .disabled(0), .enable("false")) decoder_1 (
    .out0(decoder_1_out0), .out1(AluOp), .out2(AluY), .out3(WriteM), .out4(decoder_1_out4),
    .out5(decoder_1_out5), .out6(decoder_1_out6), .sel(register_3_q_2));  // open: out7
  Multiplexer #(.width(8), .enable("false")) multiplexer_2 (
    .in0(register_4_q), .in1({8{1'b0}}), .out(multiplexer_2_out), .sel(AluY));
  // Probe on multiplexer_2_out
  // Probe on multiplexer_2_out
  // Probe on multiplexer_2_out
  // Probe on ram_1_data
  // Probe on ram_1_data
  // Probe on ram_1_data
  or or_1 (WriteF, decoder_1_out0, AluOp);
  or or_2 (WriteR, decoder_1_out0, AluOp, AluY);
  or or_3 (JMP, decoder_1_out4, and_1_out, and_2_out);
  and and_1 (and_1_out, decoder_1_out5, FZ);
  and and_2 (and_2_out, decoder_1_out6, FC);
  // Probe on sumador_restador_con_flags_1_resultado
  // Probe on sumador_restador_con_flags_1_resultado
  // Probe on sumador_restador_con_flags_1_resultado
  Sumador_Restador_con_flags sumador_restador_con_flags_1 (
    .Op(AluOp), .A(multiplexer_2_out), .B(ram_1_data), .Acarreo__Carry(C), .Cero__Zero(Z),
    .Resultado(sumador_restador_con_flags_1_resultado));

  // Other names for the same wires on the sheet: SelPC_Data = Clock

  // Notes on the sheet:
  //   Tipo
  //   Procesamiento de datos
  //   Transferencia
  //   Control de flujo
  //   Load
  //   Set de instrucciones
  //   PC
  //   PC =  PC + 1
  //   Sintaxis
  //   ADD [dirección]
  //   SUB [dirección]
  //   LDA [dirección]
  //   STA [dirección]
  //   JMP  Dirección
  //   JZ     Dirección
  //   JC     Dirección
  //   La instrucción JC salta si el registro C tiene valor 1 
  //   Dirección
  //   LDA [4]
  //   0
  //   1
  //   JZ  0
  //   2
  //   3
  //   4
  //   5
  //   Sim-AC-8-Von Neumann
  //   CodeOp
  //   000
  //   0 =
  //   001
  //   1 =
  //   2 =
  //   010
  //   3 =
  //   011
  //   4 =
  //   100
  //   5 =
  //   101
  //   6 =
  //   110
  //    = 0x44 hex
  //   SUB [5]
  //    = 0x25 hex
  //    = 0xA0 hex
  //   JMP 0
  //    = 0x80 hex
  //   0x02 hex
  //   0x03 hex
  //   AluY
  //   0
  //   0
  //   1
  //   0
  //   0
  //   0
  //   0
  //   Z
  //   Memoria de instrucciones y datos
  //   ProgramaAC-VonNeumann.mem
  //   ALUOp
  //   WriteR
  //   0
  //   1
  //   1
  //   1
  //   0
  //   1
  //   0
  //   0
  //   0
  //   0
  //   0
  //   0
  //   0
  //   0
  //   WriteM
  //   0
  //   0
  //   0
  //   1
  //   0
  //   0
  //   0
  //   C
  //   IR
  //   JMP
  //   WriteF
  //   0
  //   1
  //   1
  //   0
  //   0
  //   0
  //   1
  //   0
  //   1
  //   0
  //   1
  //   0
  //   0
  //   1
  //   CodeOp
  //   AC
  //   Formato Instrucción
  //   CodeOp
  //   Unidad de Control
  //   Dirección
  //   | b7 b6 b5 | b4 b3 b2 b1 b0 | 
  //   (byte 1)
  //    Habilitación escritura registro AC
  //    Habilitación escritura en memoria
endmodule

module Sim_AC_9_Harvard (
  input  Clock
);

  wire AluOp, AluX, AluY, and_1_out, and_2_out, and_3_out, C, decoder_1_out0, decoder_1_out4, decoder_1_out5,
       decoder_1_out6, FC, FZ, HLT, JMP, not_1_out, WriteF, WriteR, Z;
  wire [4:0] counter_1_q;
  wire [7:0] multiplexer_1_out, multiplexer_2_out, ram_1_data, ram_2_data, register_3_q,
       sumador_restador_con_flags_1_resultado;

  not not_1 (not_1_out, JMP);
  and and_1 (and_1_out, Clock, ~HLT);  // AND_Gate
  Counter #(.width(5), .max('h1f), .trigger("falling")) counter_1 (
    .load(JMP), .D(ram_1_data[4:0]), .count(not_1_out), .Q(counter_1_q), .clk(and_1_out));  // open: carry, clr
  // Probe on counter_1_q
  // Probe on counter_1_q
  Register #(.width(1)) register_1 (.D(Z), .en(WriteF), .Q(FZ), .clk(Clock));  // open: clr
  RAM #(.addrWidth(5)) ram_1 (.addr(counter_1_q), .data(ram_1_data));  // open: sel, clk, ld, clr
  // Probe on ram_1_data[4:0]
  // Probe on ram_1_data[4:0]
  // Probe on ram_1_data[7:5]
  // Probe on ram_1_data[7:5]
  Register #(.width(1)) register_2 (.D(C), .en(WriteF), .Q(FC), .clk(Clock));  // open: clr
  Decoder #(.select(3), .enable("false")) decoder_1 (
    .out0(decoder_1_out0), .out1(AluOp), .out2(AluY), .out3(AluX), .out4(decoder_1_out4),
    .out5(decoder_1_out5), .out6(decoder_1_out6), .out7(HLT), .sel(ram_1_data[7:5]));
  Register register_3 (
    .D(sumador_restador_con_flags_1_resultado), .en(WriteR), .Q(register_3_q), .clk(Clock));  // open: clr
  Multiplexer #(.width(8), .enable("false")) multiplexer_1 (
    .in0(register_3_q), .in1({8{1'b0}}), .out(multiplexer_1_out), .sel(AluY));
  Multiplexer #(.width(8), .enable("false")) multiplexer_2 (
    .in0(ram_2_data), .in1({8{1'b0}}), .out(multiplexer_2_out), .sel(AluX));
  or or_1 (WriteR, decoder_1_out0, AluOp, AluY);
  and and_2 (and_2_out, decoder_1_out5, FZ);
  and and_3 (and_3_out, decoder_1_out6, FC);
  // Probe on multiplexer_1_out
  // Probe on multiplexer_1_out
  // Probe on multiplexer_1_out
  // Probe on multiplexer_2_out
  // Probe on multiplexer_2_out
  // Probe on multiplexer_2_out
  or or_2 (WriteF, decoder_1_out0, AluOp);
  or or_3 (JMP, decoder_1_out4, and_2_out, and_3_out);
  // Probe on sumador_restador_con_flags_1_resultado
  // Probe on sumador_restador_con_flags_1_resultado
  // Probe on sumador_restador_con_flags_1_resultado
  Sumador_Restador_con_flags sumador_restador_con_flags_1 (
    .Op(AluOp), .A(multiplexer_1_out), .B(multiplexer_2_out), .Acarreo__Carry(C), .Cero__Zero(Z),
    .Resultado(sumador_restador_con_flags_1_resultado));
  RAM #(.addrWidth(5), .bus("separate")) ram_2 (
    .addr(ram_1_data[4:0]), .din(sumador_restador_con_flags_1_resultado), .data(ram_2_data), .str(AluX),
    .clk(Clock));  // open: sel, ld, clr

  // Other names for the same wires on the sheet: WriteMD = AluX

  // Notes on the sheet:
  //   Tipo
  //   Procesamiento de datos
  //   Transferencia
  //   Control de flujo
  //   Set de instrucciones
  //   Load
  //   Sintaxis
  //   ADD [Dirección]
  //   SUB [Dirección]
  //   LDA [Dirección]
  //   STA [Dirección]
  //   JMP  Dirección
  //   JZ     Dirección
  //   JC    Dirección
  //   HLT
  //   PC
  //   PC =  PC + 1
  //   0
  //   1
  //   2
  //   3
  //   Sim-AC-9-Harvard
  //   CodeOp
  //   000
  //   0 =
  //   001
  //   1 =
  //   2 =
  //   010
  //   3 =
  //   011
  //   4 =
  //   100
  //   5 =
  //   101
  //   6 =
  //   110
  //   7 =
  //   111
  //   Memoria de instrucciones
  //   ProgramaAC-4.mem
  //   LDA [0]
  //   SUB [1]
  //   JZ  0
  //   HLT
  //   AluY
  //   0
  //   0
  //   1
  //   0
  //   0
  //   0
  //   0
  //   0
  //   Z
  //    = 0x40 hex
  //    = 0x21 hex
  //    = 0xA0 hex
  //    = 0xE0 hex
  //   ALUOp
  //   AluX
  //   0
  //   0
  //   0
  //   1
  //   0
  //   0
  //   0
  //   1
  //   0
  //   0
  //   0
  //   0
  //   0
  //   0
  //   0
  //   0
  //   C
  //   Dirección
  //   CodeOp
  //   WriteR
  //   WriteMD
  //   1
  //   0
  //   1
  //   0
  //   1
  //   0
  //   0
  //   1
  //   0
  //   0
  //   0
  //   0
  //   0
  //   0
  //   0
  //   0
  //   JMP
  //   0
  //   0
  //   0
  //   1
  //   1
  //   1
  //   1
  //   0
  //   WriteF
  //   1
  //   1
  //   0
  //   0
  //   0
  //   0
  //   0
  //   0
  //   AC
  //   Unidad de Control
  //   Formato Instrucción
  //   CodeOp
  //   | b7 b6 b5 | b4 b3 b2 b1 b0 | 
  //   (byte 1)
  //   Dirección
  //   0x02 hex
  //   0
  //   0x03 hex
  //   1
  //   Memoria de datos
  //   DatosAC-4.mem
endmodule

module Sim_AC_9_Von_Neumann (
  input  Clock
);

  wire AluOp, AluY, and_1_out, and_2_out, and_3_out, C, decoder_1_out0, decoder_1_out4, decoder_1_out5,
       decoder_1_out6, FC, FZ, HLT, JMP, not_1_out, not_2_out, WriteF, WriteM, WriteR, Z;
  wire [4:0] counter_1_q, multiplexer_1_out, register_3_q;
  wire [7:0] multiplexer_2_out, ram_1_data, register_4_q, sumador_restador_con_flags_1_resultado;
  wire [7:5] register_3_q_2;

  not not_1 (not_1_out, JMP);
  and and_1 (and_1_out, Clock, ~HLT);  // AND_Gate
  Counter #(.width(5), .max('h1f), .trigger("falling")) counter_1 (
    .load(JMP), .D(register_3_q), .count(not_1_out), .Q(counter_1_q), .clk(and_1_out));  // open: carry, clr
  // Probe on counter_1_q
  // Probe on counter_1_q
  // Probe on register_3_q
  // Probe on register_3_q
  Multiplexer #(.width(5), .enable("false")) multiplexer_1 (
    .in0(counter_1_q), .in1(register_3_q), .out(multiplexer_1_out), .sel(Clock));
  not not_2 (not_2_out, Clock);
  Register #(.width(1), .trigger("falling")) register_1 (.D(Z), .en(WriteF), .Q(FZ), .clk(Clock));  // open: clr
  RAM #(.addrWidth(5), .bus("separate")) ram_1 (
    .addr(multiplexer_1_out), .din(register_4_q), .data(ram_1_data), .str(WriteM), .clk(not_2_out));  // open: sel, ld, clr
  Register #(.width(1), .trigger("falling")) register_2 (.D(C), .en(WriteF), .Q(FC), .clk(Clock));  // open: clr
  Register register_3 (.D(ram_1_data), .Q({register_3_q_2, register_3_q}), .clk(Clock));  // open: en, clr
  // Probe on register_3_q_2
  // Probe on register_3_q_2
  Register #(.trigger("falling")) register_4 (
    .D(sumador_restador_con_flags_1_resultado), .en(WriteR), .Q(register_4_q), .clk(Clock));  // open: clr
  Decoder #(.select(3), .disabled(0), .enable("false")) decoder_1 (
    .out0(decoder_1_out0), .out1(AluOp), .out2(AluY), .out3(WriteM), .out4(decoder_1_out4),
    .out5(decoder_1_out5), .out6(decoder_1_out6), .out7(HLT), .sel(register_3_q_2));
  Multiplexer #(.width(8), .enable("false")) multiplexer_2 (
    .in0(register_4_q), .in1({8{1'b0}}), .out(multiplexer_2_out), .sel(AluY));
  // Probe on multiplexer_2_out
  // Probe on multiplexer_2_out
  // Probe on multiplexer_2_out
  // Probe on ram_1_data
  // Probe on ram_1_data
  // Probe on ram_1_data
  or or_1 (WriteF, decoder_1_out0, AluOp);
  or or_2 (WriteR, decoder_1_out0, AluOp, AluY);
  or or_3 (JMP, decoder_1_out4, and_2_out, and_3_out);
  and and_2 (and_2_out, decoder_1_out5, FZ);
  and and_3 (and_3_out, decoder_1_out6, FC);
  // Probe on sumador_restador_con_flags_1_resultado
  // Probe on sumador_restador_con_flags_1_resultado
  // Probe on sumador_restador_con_flags_1_resultado
  Sumador_Restador_con_flags sumador_restador_con_flags_1 (
    .Op(AluOp), .A(multiplexer_2_out), .B(ram_1_data), .Acarreo__Carry(C), .Cero__Zero(Z),
    .Resultado(sumador_restador_con_flags_1_resultado));

  // Other names for the same wires on the sheet: SelPC_Data = Clock

  // Notes on the sheet:
  //   Tipo
  //   Procesamiento de datos
  //   Transferencia
  //   Control de flujo
  //   Load
  //   Set de instrucciones
  //   PC
  //   PC =  PC + 1
  //   Sintaxis
  //   ADD [Dirección]
  //   SUB [Dirección]
  //   LDA [Dirección]
  //   STA [Dirección]
  //   JMP  Dirección
  //   JZ     Dirección
  //   JC    Dirección
  //   HLT
  //   Dirección
  //   LDA [4]
  //   0
  //   1
  //   JZ 0
  //   2
  //   HLT
  //   3
  //   4
  //   5
  //   Sim-AC-9-Von Neumann
  //   CodeOp
  //   000
  //   0 =
  //   001
  //   1 =
  //   2 =
  //   010
  //   3 =
  //   011
  //   4 =
  //   100
  //   5 =
  //   101
  //   6 =
  //   110
  //   7 =
  //   111
  //    = 0x44 hex
  //   SUB [5]
  //    = 0x25 hex
  //    = 0xA0 hex
  //    = 0xE0 hex
  //   0x02 hex
  //   0x03 hex
  //   AluY
  //   0
  //   0
  //   1
  //   0
  //   0
  //   0
  //   0
  //   0
  //   Z
  //   Memoria de instrucciones y datos
  //   ProgramaAC-VonNeumann.mem
  //   WriteR
  //   ALUOp
  //   0
  //   1
  //   1
  //   1
  //   0
  //   1
  //   0
  //   0
  //   0
  //   0
  //   0
  //   0
  //   0
  //   0
  //   0
  //   0
  //   WriteM
  //   0
  //   0
  //   0
  //   1
  //   0
  //   0
  //   0
  //   0
  //   C
  //   IR
  //   WriteF
  //   JMP
  //   1
  //   0
  //   1
  //   0
  //   0
  //   0
  //   0
  //   1
  //   1
  //   0
  //   1
  //   0
  //   0
  //   1
  //   0
  //   0
  //   CodeOp
  //   AC
  //   Formato Instrucción
  //   CodeOp
  //   Unidad de Control
  //   Dirección
  //   | b7 b6 b5 | b4 b3 b2 b1 b0 | 
  //   (byte 1)
  //    Habilitación escritura registro AC
  //    Habilitación escritura en memoria
endmodule
